// Digital circuit descodificador2x4.dig as structural Verilog
module descodificador2x4 (
  input  Bit1,
  input  Bit0,
  input  En0,
  input  En1,
  input  En2,
  input  En3,
  output Out0,
  output Out1,
  output Out2,
  output Out3
);

  and and_1 (Out0, ~Bit1, ~Bit0, En0);  // And
  and and_2 (Out1, ~Bit1, Bit0, En1);  // And
  and and_3 (Out2, Bit1, ~Bit0, En2);  // And
  and and_4 (Out3, Bit1, Bit0, En3);
endmodule
